# Fritzing sketch Circuit (saved by Fritzing 0.9.3b)
breadboards: 1

parts:
  R1 = Resistor [tolerance=±5% resistance=220 package=THT]
  Gizwits_WiFi_Witty_ESP-12F1 = Gizwits WiFi Witty ESP-12F
  R2 = Resistor [tolerance=±5% resistance=220 package=THT]
  R3 = Resistor [tolerance=±5% resistance=220 package=THT]
  U1 = TLP621 [package=THT]

nets:
  N1: R1.Pin_0, Gizwits_WiFi_Witty_ESP-12F1.RXD, U1.Pin_4
  N2: R1.Pin_1, R2.Pin_0
  N3: Gizwits_WiFi_Witty_ESP-12F1.VCC, R2.Pin_1
  N4: Gizwits_WiFi_Witty_ESP-12F1.GND, U1.Pin_3
  N5: R3.Pin_0, U1.Pin_1
